// Logisim project MIPSProcessor.circ as structural Verilog
module MIPS32 (
);

  wire clock_1_out, exmem_1_moveout, exmem_1_skipout, idex_1_iout, idex_1_luiout, idex_1_movnout,
       idex_1_movzout, idex_1_skipout, idex_1_sltiout, idex_1_sltiuout, idex_1_sltout, idex_1_sltuout,
       instrcutionwriteback_1_we, instructiondecode_1_i, instructiondecode_1_lui, instructiondecode_1_movn,
       instructiondecode_1_movz, instructiondecode_1_skipout, instructiondecode_1_slt,
       instructiondecode_1_slti, instructiondecode_1_sltiu, instructiondecode_1_sltu,
       instructionexcute_1_moveout, instructionexcute_1_skipout, instructionmemory_1_moveout,
       instructionmemory_1_skipout, memwb_1_moveout, memwb_1_skipout, not_1_out, not_2_out;
  wire [1:0] hazards_1_hazarda, hazards_1_hazardb;
  wire [3:0] idex_1_ctrlout, instructiondecode_1_ctrl;
  wire [4:0] exmem_1_rdout, idex_1_rdout, idex_1_rsout, idex_1_rtout, idex_1_saout,
       instrcutionwriteback_1_rdout, instructiondecode_1_rdout, instructiondecode_1_rsout,
       instructiondecode_1_rtout, instructiondecode_1_sa, instructionexcute_1_rdout,
       instructionmemory_1_rdout, memwb_1_rdout;
  wire [31:0] exmem_1_aout, exmem_1_dout, idex_1_aout, idex_1_bout, idex_1_immout, ifid_1_instout,
       ifid_1_pcplus4out, instrcutionwriteback_1_result, instructiondecode_1_a, instructiondecode_1_b,
       instructiondecode_1_imm, instructiondecode_1_pcplus4out, instructionexcute_1_aout,
       instructionexcute_1_d, instructionfetch_1_inst, instructionfetch_1_pcplus4, instructionmemory_1_aout,
       instructionmemory_1_dout, memwb_1_aout, memwb_1_dout, multiplexer_1_out, multiplexer_2_out,
       multiplexer_3_out, multiplexer_4_out;

  Clock clock_1 (.out(clock_1_out));
  instructionFetch instructionfetch_1 (
    .clck(clock_1_out), .inst(instructionfetch_1_inst), .PCPlus4(instructionfetch_1_pcplus4));
  IFID ifid_1 (
    .inst(instructionfetch_1_inst), .PCPlus4(instructionfetch_1_pcplus4), .clck(clock_1_out),
    .instOut(ifid_1_instout), .PCPlus4Out(ifid_1_pcplus4out));
  instructionDecode instructiondecode_1 (
    .D(instrcutionwriteback_1_result), .skip(instrcutionwriteback_1_we), .clck(clock_1_out),
    .inst(ifid_1_instout), .PCPlus4(ifid_1_pcplus4out), .rd(instrcutionwriteback_1_rdout),
    .A(instructiondecode_1_a), .B(instructiondecode_1_b), .rdOut(instructiondecode_1_rdout),
    .Sa(instructiondecode_1_sa), .imm(instructiondecode_1_imm), .SLTIU(instructiondecode_1_sltiu),
    .ctrl(instructiondecode_1_ctrl), .SLTI(instructiondecode_1_slti), .I(instructiondecode_1_i),
    .SLTU(instructiondecode_1_sltu), .SLT(instructiondecode_1_slt), .skipOut(instructiondecode_1_skipout),
    .LUI(instructiondecode_1_lui), .MOVN(instructiondecode_1_movn), .MOVZ(instructiondecode_1_movz),
    .PCPlus4out(instructiondecode_1_pcplus4out), .rtOut(instructiondecode_1_rtout),
    .rsOut(instructiondecode_1_rsout));
  not not_1 (not_1_out, exmem_1_skipout);
  IDEX idex_1 (
    .A(instructiondecode_1_a), .B(instructiondecode_1_b), .Sa(instructiondecode_1_sa),
    .imm(instructiondecode_1_imm), .SLTIU(instructiondecode_1_sltiu), .ctrl(instructiondecode_1_ctrl),
    .SLTI(instructiondecode_1_slti), .I(instructiondecode_1_i), .clck(clock_1_out),
    .SLTU(instructiondecode_1_sltu), .SLT(instructiondecode_1_slt), .skip(instructiondecode_1_skipout),
    .LUI(instructiondecode_1_lui), .MOVN(instructiondecode_1_movn), .MOVZ(instructiondecode_1_movz),
    .PCPlus4(instructiondecode_1_pcplus4out), .rd(instructiondecode_1_rdout), .rt(instructiondecode_1_rtout),
    .rs(instructiondecode_1_rsout), .Aout(idex_1_aout), .Bout(idex_1_bout), .SaOut(idex_1_saout),
    .immOut(idex_1_immout), .SLTIUout(idex_1_sltiuout), .ctrlOut(idex_1_ctrlout), .SLTIout(idex_1_sltiout),
    .Iout(idex_1_iout), .SLTUout(idex_1_sltuout), .SLTout(idex_1_sltout), .skipOut(idex_1_skipout),
    .LUIout(idex_1_luiout), .MOVNout(idex_1_movnout), .MOVZout(idex_1_movzout), .rdOut(idex_1_rdout),
    .rtOut(idex_1_rtout), .rsOut(idex_1_rsout));
  not not_2 (not_2_out, memwb_1_skipout);
  instructionExcute instructionexcute_1 (
    .A(multiplexer_3_out), .B(multiplexer_1_out), .Sa(idex_1_saout), .imm(idex_1_immout),
    .SLTIU(idex_1_sltiuout), .ctrl(idex_1_ctrlout), .SLTI(idex_1_sltiout), .I(idex_1_iout),
    .SLTU(idex_1_sltuout), .SLT(idex_1_sltout), .skip(idex_1_skipout), .LUI(idex_1_luiout),
    .MOVN(idex_1_movnout), .MOVZ(idex_1_movzout), .rd(idex_1_rdout), .Aout(instructionexcute_1_aout),
    .D(instructionexcute_1_d), .moveOut(instructionexcute_1_moveout), .skipOut(instructionexcute_1_skipout),
    .rdOut(instructionexcute_1_rdout));
  Hazards hazards_1 (
    .IDEXrt(idex_1_rtout), .IDEXrs(idex_1_rsout), .EXMEMrd(exmem_1_rdout), .EXMEMregWrite(not_1_out),
    .MEMWBrd(memwb_1_rdout), .MEMWBregWrite(not_2_out), .HazardA(hazards_1_hazarda),
    .HazardB(hazards_1_hazardb));
  EXMEM exmem_1 (
    .A(instructionexcute_1_aout), .D(instructionexcute_1_d), .clck(clock_1_out),
    .move(instructionexcute_1_moveout), .skip(instructionexcute_1_skipout), .rd(instructionexcute_1_rdout),
    .Aout(exmem_1_aout), .Dout(exmem_1_dout), .moveOut(exmem_1_moveout), .skipOut(exmem_1_skipout),
    .rdOut(exmem_1_rdout));
  Multiplexer #(.width(32), .enable("false")) multiplexer_1 (
    .in0(multiplexer_2_out), .in1(exmem_1_dout), .out(multiplexer_1_out), .sel(hazards_1_hazardb[1]));
  instructionMemory instructionmemory_1 (
    .A(exmem_1_aout), .D(exmem_1_dout), .move(exmem_1_moveout), .skip(exmem_1_skipout), .rd(exmem_1_rdout),
    .Aout(instructionmemory_1_aout), .Dout(instructionmemory_1_dout), .moveOut(instructionmemory_1_moveout),
    .skipOut(instructionmemory_1_skipout), .rdOut(instructionmemory_1_rdout));
  Multiplexer #(.width(32), .enable("false")) multiplexer_2 (
    .in0(idex_1_bout), .in1(memwb_1_dout), .out(multiplexer_2_out), .sel(hazards_1_hazardb[0]));
  Multiplexer #(.width(32), .enable("false")) multiplexer_3 (
    .in0(multiplexer_4_out), .in1(exmem_1_dout), .out(multiplexer_3_out), .sel(hazards_1_hazarda[1]));
  MEMWB memwb_1 (
    .A(instructionmemory_1_aout), .D(instructionmemory_1_dout), .clck(clock_1_out),
    .move(instructionmemory_1_moveout), .skip(instructionmemory_1_skipout), .rd(instructionmemory_1_rdout),
    .Aout(memwb_1_aout), .Dout(memwb_1_dout), .moveOut(memwb_1_moveout), .skipOut(memwb_1_skipout),
    .rdOut(memwb_1_rdout));
  Multiplexer #(.width(32), .enable("false")) multiplexer_4 (
    .in0(idex_1_aout), .in1(memwb_1_dout), .out(multiplexer_4_out), .sel(hazards_1_hazarda[0]));
  instrcutionWriteback instrcutionwriteback_1 (
    .A(memwb_1_aout), .D(memwb_1_dout), .move(memwb_1_moveout), .rd(memwb_1_rdout), .skip(memwb_1_skipout),
    .result(instrcutionwriteback_1_result), .rdOut(instrcutionwriteback_1_rdout),
    .WE(instrcutionwriteback_1_we));
endmodule

module instructionFetch (
  input  clck,
  output [31:0] inst,
  output [31:0] PCPlus4
);

  wire incrementer_1_p1;
  wire [31:2] register_1_q;

  Register #(.width(32)) register_1 (
    .D(PCPlus4), .en(incrementer_1_p1), .clk(clck), .Q({register_1_q, PCPlus4[1:0]}));  // open: clr
  // Incrementer #(.width(30)) incrementer_1: pin names not known; wires that end beside it: incrementer_1_p1, register_1_q, PCPlus4[31:2]
  // MIPSProgramROM mipsprogramrom_1: pin names not known; wires that end beside it: {register_1_q, PCPlus4[1:0]}, inst

  // Notes on the sheet:
  //   contents of mipsprogramrom_1 (hex, n*v repeats v):
  //   #ADDIU  ADDIU $0, $1, 5  #0, bc 0 register should stay 0  ADDIU $1, $1, 6  #6  ADDIU $2, $2, 1  #1
  //   ADDIU $3, $3, 2  #2  ADDIU $4, $4, 3  #3  ADDIU $5, $0, 2  #2  ADDIU $6, $6, 1000 #1000  ADDIU $7,
  //   $1, 10 #16 6+10=16  ADDIU $8, $0, 32767 #32767, max int to a zero  ADDIU $9, $2, 0 #1  ADDIU $10,
  //   $5, 32767 #? adding a max int to a nonzero value  ADDIU $11, $0, -20 #? adding negative to zero
  //   ADDIU $12, $5, -32767 #-32765 adding a min int to a nonzero value  ADDIU $13, $7, 2  #18  ADDIU $14,
  //   $7, 2  #18  #ADDIU with hazards  ADDIU $15, $13, 5  #23, WB to EX Forward  ADDIU $16, $15, 3 #26,
  //   MEM to Ex Forward  ADDIU $17, $14, 1  #19, checks that register reads on falling edge so write and
  //   read from register can happen in same cycle.  #ANDI  ANDI $18, $0, 0 #0, 0 AND 0, testing zero  ANDI
  //   $19, $4, 3 #3, 3 AND 3, testing same number  ANDI $20, $6, 1243 #200 , testing a random number(dif
  //   numbers)  #ANDI with hazards ANDI $21, $19, 1 #1? WB to EX Forward  ANDI $22, $21, 3726  #0 MEM to
  //   EX Forward  ANDI $23, $20, 2893  #72, checks that register reads on falling edge so write and read
  //   from register can happen in same cycle.  #ORI ORI $24, $0, 0 #0, 0 OR 0, testing zero  ORI $25, $20,
  //   200 #200, 200 OR 200, testing same number  ORI $26, $1, 1243 #1247 , testing a random number(dif
  //   numbers)  ORI $27, $19, 4 #7, no similar bits  #ORI with hazards ORI $28, $25, 1 #201 WB to EX
  //   Forward  ORI $29, $27, 782  #975 MEM to EX Forward  ORI $30, $26, 289  #1535, checks that register
  //   reads on falling edge so write and read from register can happen in same cycle.  #XORI XORI $31, $0,
  //   0 #0, 0 OR 0, testing zero  XORI $1, $20, 200 #0, 200 XOR 200, testing same number  XORI $2, $26,
  //   5672 #? , testing a random number(dif numbers)  XORI $3, $19, 4 #7, no similar bits  #XORI with
  //   hazards XORI $4, $2, 1 #3 WB to EX Forward  XORI $5, $4, 782  #? MEM to EX Forward  XORI $6, $3, 989
  //   #?, checks that register reads on falling edge so write and read from register can happen in same
  //   cycle.  #SLTI SLTI $7, $29, 975  #0 equal  SLTI $8, $30, 2987  #1 less than  SLTI $9, $27, 5  #0
  //   greater than  #SLTI with hazards SLTI $10, $8, 2757  #? WB to EX Forward  SLTI $11, $10, 2987  #?,
  //   MEM to EX Forward  SLTI $12, $9, 56  #?, checks that register reads on falling edge so write and
  //   read from register can happen in same cycle.  #SLTIU SLTIU $13, $29, 975  #0 equal  SLTI $14, $30,
  //   2987  #1 less than  SLTI $15, $27, 5  #0 greater than  #SLTIU with hazards SLTI $16, $14, 2757  #?
  //   WB to EX Forward  SLTI $17, $16, 2987  #?, MEM to EX Forward  SLTI $18, $15, 56  #?, checks that
  //   register reads on falling edge so write and read from register can happen in same cycle.  #R-Type
  //   #ADDU  ADDIU $19, $0, 32767 #32767, max int to a zero, using this op to test later op  ADDU $20,
  //   $27, $30 #? adding 2 dif non zeros  ADDU $21, $0, $0 #0, adding zeros  ADDU $22, $0, $4 #3 adding
  //   pos to zero  ADDU $23, $19, $3 #max int plus positive  #ADDU with hazards  ADDU $24, $22, $16  #?,
  //   WB to EX Forward  ADDU $25, $24, $17 #?, MEM to Ex Forward  ADDU $26, $23, $18  #?, checks that
  //   register reads on falling edge so write and read from register can happen in same cycle.  ADDU $27,
  //   $25, $26 #? double forwarding  ADDU $28, $1, $2 #? for future test  ADDU $28, $3, $4 #? for next
  //   test  ADDU $29, $28, $5 #? testing that mem to ex forwarding is prioritized over wb to ex
  //   forwarding.
endmodule

module instructionDecode (
  input  [31:0] D,
  input  skip,
  input  clck,
  input  [31:0] inst,
  input  [31:0] PCPlus4,
  input  [4:0] rd,
  output [31:0] A,
  output [31:0] B,
  output [4:0] rdOut,
  output [4:0] Sa,
  output [31:0] imm,
  output SLTIU,
  output [3:0] ctrl,
  output SLTI,
  output I,
  output SLTU,
  output SLT,
  output skipOut,
  output LUI,
  output MOVN,
  output MOVZ,
  output [31:0] PCPlus4out,
  output [4:0] rtOut,
  output [4:0] rsOut
);

  wire decode_1_var, or_1_out;
  wire [4:0] decode_1_saout;

  decode decode_1 (
    .Instruction(inst), .SLTIU(SLTIU), .SLTI(SLTI), .I(I), .ctrl(ctrl), .Var(decode_1_var),
    .SaOut(decode_1_saout), .SLTU(SLTU), .SLT(SLT), .skip(skipOut), .Imm(imm), .LUI(LUI), .MOVN(MOVN),
    .MOVZ(MOVZ));
  // RegisterFile #(.trigger("falling")) registerfile_1: pin names not known; wires that end beside it: D, clck, skip, rd, inst[25:21], inst[20:16], A, B
  or or_1 (or_1_out, I, LUI);
  Multiplexer #(.width(5), .enable("false")) multiplexer_1 (
    .in0(inst[15:11]), .in1(inst[20:16]), .out(rdOut), .sel(or_1_out));
  Multiplexer #(.width(5), .enable("false")) multiplexer_2 (
    .in0(decode_1_saout), .in1(A[4:0]), .out(Sa), .sel(decode_1_var));

  assign PCPlus4out = PCPlus4;
  assign rsOut = inst[25:21];
  assign rtOut = inst[20:16];
endmodule

module decode (
  input  [31:0] Instruction,
  output SLTIU,
  output SLTI,
  output I,
  output [3:0] ctrl,
  output Var,
  output [4:0] SaOut,
  output SLTU,
  output SLT,
  output skip,
  output [31:0] Imm,
  output LUI,
  output MOVN,
  output MOVZ
);

  wire and_2_out, and_3_out, itype_1_slti, itype_1_sltiu, jbranchtype_1_skip, loadstoretype_1_skip,
       not_1_out, not_2_out, not_3_out, or_1_out, or_2_out, rtype_1_jumpr, rtype_1_movn, rtype_1_movz,
       rtype_1_slt, rtype_1_sltu;
  wire [3:0] itype_1_ctrl, rtype_1_ctrl;

  Rtype rtype_1 (
    .Sa(Instruction[10:6]), .func(Instruction[5:0]), .Var(Var), .SaOut(SaOut), .ctrl(rtype_1_ctrl),
    .SLT(rtype_1_slt), .JumpR(rtype_1_jumpr), .MOVN(rtype_1_movn), .MOVZ(rtype_1_movz), .SLTU(rtype_1_sltu));
  LoadStoreType loadstoretype_1 (.Bit31(Instruction[31]), .skip(loadstoretype_1_skip));
  Itype itype_1 (
    .imm0To15(Instruction[15:0]), .Opcode26To28(Instruction[28:26]), .SLTIU(itype_1_sltiu),
    .SLTI(itype_1_slti), .ctrl(itype_1_ctrl), .Imm(Imm), .LUI(LUI));
  JBranchType jbranchtype_1 (.Bit29(Instruction[29]), .skip(jbranchtype_1_skip));
  or or_1 (or_1_out, loadstoretype_1_skip, jbranchtype_1_skip);
  Multiplexer #(.width(4), .enable("false")) multiplexer_1 (
    .in0(rtype_1_ctrl), .in1(itype_1_ctrl), .out(ctrl), .sel(or_2_out));
  or or_2 (or_2_out, Instruction[26], Instruction[27], Instruction[28], Instruction[29], Instruction[30], Instruction[31]);
  not not_1 (not_1_out, or_2_out);
  and and_1 (I, or_2_out, not_3_out);
  not not_2 (not_2_out, or_2_out);
  and and_2 (and_2_out, or_2_out, or_1_out);
  and and_3 (and_3_out, not_1_out, rtype_1_jumpr);
  and and_4 (SLTIU, itype_1_sltiu, I);
  and and_5 (SLTI, I, itype_1_slti);
  and and_6 (SLTU, rtype_1_sltu, not_2_out);
  and and_7 (SLT, not_2_out, rtype_1_slt);
  not not_3 (not_3_out, skip);
  or or_3 (skip, and_2_out, and_3_out);
  and and_8 (MOVN, not_1_out, rtype_1_movn);
  and and_9 (MOVZ, not_1_out, rtype_1_movz);
endmodule

module Rtype (
  input  [4:0] Sa,
  input  [5:0] func,
  output Var,
  output [4:0] SaOut,
  output [3:0] ctrl,
  output SLT,
  output JumpR,
  output MOVN,
  output MOVZ,
  output SLTU
);

  wire and_3_out, and_5_out, not_1_out, not_2_out, not_3_out, not_4_out, or_1_out, rtype1ops_1_slt,
       rtype1ops_1_sltu, shift_1_var;
  wire [3:0] rtype1ops_1_ctrl, shift_1_ctrl;

  shift shift_1 (.func0to3(func[3:0]), .Sa(Sa), .Var(shift_1_var), .ctrl(shift_1_ctrl), .Saout(SaOut));
  Rtype1Ops rtype1ops_1 (.func0to3(func[3:0]), .SLTU(rtype1ops_1_sltu), .SLT(rtype1ops_1_slt), .ctrl(rtype1ops_1_ctrl));
  not not_1 (not_1_out, func[5]);
  Multiplexer #(.width(4), .enable("false")) multiplexer_1 (
    .in0(shift_1_ctrl), .in1(rtype1ops_1_ctrl), .out(ctrl), .sel(func[5]));
  not not_2 (not_2_out, func[1]);
  and and_1 (SLTU, func[5], rtype1ops_1_sltu);
  and and_2 (SLT, rtype1ops_1_slt, func[5]);
  not not_3 (not_3_out, func[0]);
  or or_1 (or_1_out, SLTU, SLT);
  not not_4 (not_4_out, or_1_out);
  and and_3 (and_3_out, not_4_out, func[3]);
  and and_4 (Var, not_1_out, shift_1_var);
  and and_5 (and_5_out, and_3_out, func[1]);
  and and_6 (JumpR, and_3_out, not_2_out);
  and and_7 (MOVN, func[0], and_5_out);
  and and_8 (MOVZ, and_5_out, not_3_out);
endmodule

module Itype (
  input  [15:0] imm0To15,
  input  [2:0] Opcode26To28,
  output SLTIU,
  output SLTI,
  output [3:0] ctrl,
  output [31:0] Imm,
  output LUI
);

  wire and_1_out, not_1_out, not_2_out, signextended_1_slt, zeroextended_1_lui;
  wire [3:0] signextended_1_ctrl, zeroextended_1_ctrl;
  wire [31:0] signextended_1_immsigned, zeroextended_1_immzero;

  SignExtended signextended_1 (
    .OpCode26To28(Opcode26To28), .imm0To15(imm0To15), .SLT(signextended_1_slt), .ctrl(signextended_1_ctrl),
    .immSigned(signextended_1_immsigned));
  ZeroExtended zeroextended_1 (
    .OpCode26To28(Opcode26To28), .imm0To15(imm0To15), .LUI(zeroextended_1_lui), .ctrl(zeroextended_1_ctrl),
    .immZero(zeroextended_1_immzero));
  not not_1 (not_1_out, Opcode26To28[2]);
  Multiplexer #(.width(4), .enable("false")) multiplexer_1 (
    .in0(signextended_1_ctrl), .in1(zeroextended_1_ctrl), .out(ctrl), .sel(Opcode26To28[2]));
  and and_1 (and_1_out, signextended_1_slt, not_1_out);
  and and_2 (LUI, Opcode26To28[2], zeroextended_1_lui);
  not not_2 (not_2_out, Opcode26To28[0]);
  Multiplexer #(.width(32), .enable("false")) multiplexer_2 (
    .in0(signextended_1_immsigned), .in1(zeroextended_1_immzero), .out(Imm), .sel(Opcode26To28[2]));
  and and_3 (SLTIU, Opcode26To28[0], and_1_out);
  and and_4 (SLTI, not_2_out, and_1_out);
endmodule

module shift (
  input  [3:0] func0to3,
  input  [4:0] Sa,
  output Var,
  output [3:0] ctrl,
  output [4:0] Saout
);

  wire [3:0] shiftsa_1_ctrl, shiftvariable_1_ctrl;

  shiftSa shiftsa_1 (.func0to3(func0to3), .Sa(Sa), .ctrl(shiftsa_1_ctrl), .Saout(Saout));
  shiftVariable shiftvariable_1 (.funct0to3(func0to3), .ctrl(shiftvariable_1_ctrl));
  Multiplexer #(.width(4), .enable("false")) multiplexer_1 (
    .in0(shiftsa_1_ctrl), .in1(shiftvariable_1_ctrl), .out(ctrl), .sel(func0to3[2]));

  assign Var = func0to3[2];
endmodule

module shiftVariable (
  input  [3:0] funct0to3,
  output [3:0] ctrl
);


  assign ctrl = {funct0to3[3], funct0to3[1], funct0to3[3], funct0to3[0]};
endmodule

module shiftSa (
  input  [3:0] func0to3,
  input  [4:0] Sa,
  output [3:0] ctrl,
  output [4:0] Saout
);


  assign ctrl = {func0to3[3], func0to3[1], func0to3[2], func0to3[0]};
  assign Saout = Sa;
endmodule

module Rtype1Ops (
  input  [3:0] func0to3,
  output SLTU,
  output SLT,
  output [3:0] ctrl
);

  wire not_1_out;

  and and_1 (SLTU, func0to3[0], func0to3[3]);
  not not_1 (not_1_out, func0to3[0]);
  and and_2 (SLT, not_1_out, func0to3[3]);

  assign ctrl = {func0to3[2:0], func0to3[3]};
endmodule

module SignExtended (
  input  [2:0] OpCode26To28,
  input  [15:0] imm0To15,
  output SLT,
  output [3:0] ctrl,
  output [31:0] immSigned
);

  assign immSigned[31:15] = {{16{imm0To15[15]}}, imm0To15[15]};  // Bit_Extender bit_extender_1

  assign ctrl = {OpCode26To28, OpCode26To28[2]};
  assign immSigned[14:0] = imm0To15[14:0];
  assign SLT = OpCode26To28[1];
endmodule

module ZeroExtended (
  input  [2:0] OpCode26To28,
  input  [15:0] imm0To15,
  output LUI,
  output [3:0] ctrl,
  output [31:0] immZero
);

  not not_1 (ctrl[0], OpCode26To28[2]);
  assign immZero[31:16] = {{15{ctrl[0]}}, ctrl[0]};  // Bit_Extender bit_extender_1
  and and_1 (LUI, OpCode26To28[1], OpCode26To28[0]);

  assign ctrl[3:1] = OpCode26To28;
  assign immZero[15:0] = imm0To15;
endmodule

module JBranchType (
  input  Bit29,
  output skip
);

  not not_1 (skip, Bit29);
endmodule

module LoadStoreType (
  input  Bit31,
  output skip
);


  assign skip = Bit31;
endmodule

module instructionExcute (
  input  [31:0] A,
  input  [31:0] B,
  input  [4:0] Sa,
  input  [31:0] imm,
  input  SLTIU,
  input  [3:0] ctrl,
  input  SLTI,
  input  I,
  input  SLTU,
  input  SLT,
  input  skip,
  input  LUI,
  input  MOVN,
  input  MOVZ,
  input  [4:0] rd,
  output [31:0] Aout,
  output [31:0] D,
  output moveOut,
  output skipOut,
  output [4:0] rdOut
);

  wire and_1_out, and_2_out, and_3_out, comparator_1_eq, comparator_1_lt, comparator_2_lt, not_1_out,
       not_2_out, or_1_out, or_2_out, or_3_out, or_4_out;
  wire [0:0] multiplexer_4_out;
  wire [31:0] bit_extender_1_out, mips_alu_1_p5, multiplexer_1_out, multiplexer_2_out, multiplexer_3_out,
       multiplexer_5_out;

  or or_1 (or_1_out, SLTI, SLT);
  or or_2 (or_2_out, SLTIU, SLTU);
  or or_3 (or_3_out, MOVN, MOVZ);
  Multiplexer #(.width(32), .enable("false")) multiplexer_1 (.in0(B), .in1(imm), .out(multiplexer_1_out), .sel(I));
  or or_4 (or_4_out, or_2_out, or_1_out);
  assign bit_extender_1_out = {{31{LUI}}, LUI};  // Bit_Extender bit_extender_1
  and and_1 (and_1_out, I, not_1_out);
  not not_1 (not_1_out, or_3_out);
  Multiplexer #(.width(32), .enable("false")) multiplexer_2 (
    .in0(A), .in1(bit_extender_1_out), .out(multiplexer_2_out), .sel(or_3_out));
  Multiplexer #(.width(32), .enable("false")) multiplexer_3 (
    .in0(B), .in1(imm), .out(multiplexer_3_out), .sel(and_1_out));
  // Mips_ALU mips_alu_1: pin names not known; wires that end beside it: A, multiplexer_1_out, ctrl, Sa, mips_alu_1_p5
  Comparator #(.width(32)) comparator_1 (
    .a(multiplexer_2_out), .b(multiplexer_3_out), .eq(comparator_1_eq), .lt(comparator_1_lt));  // open: gt
  Comparator #(.width(32), .mode("unsigned")) comparator_2 (
    .a(A), .b(multiplexer_3_out), .lt(comparator_2_lt));  // open: gt, eq
  Multiplexer #(.enable("false")) multiplexer_4 (
    .in0(comparator_1_lt), .in1(comparator_2_lt), .out(multiplexer_4_out[0]), .sel(or_4_out));
  not not_2 (not_2_out, comparator_1_eq);
  and and_2 (and_2_out, not_2_out, MOVN);
  and and_3 (and_3_out, MOVZ, comparator_1_eq);
  Multiplexer #(.width(32), .enable("false")) multiplexer_5 (
    .in0(mips_alu_1_p5), .in1({bit_extender_1_out[31:1], multiplexer_4_out[0]}), .out(multiplexer_5_out),
    .sel(or_4_out));
  or or_5 (moveOut, and_2_out, and_3_out);
  Multiplexer #(.width(32), .enable("false")) multiplexer_6 (
    .in0(multiplexer_5_out), .in1({imm[15:0], imm[31:16]}), .out(D), .sel(LUI));

  assign Aout = A;
  assign rdOut = rd;
  assign skipOut = skip;
endmodule

module IDEX (
  input  [31:0] A,
  input  [31:0] B,
  input  [4:0] Sa,
  input  [31:0] imm,
  input  SLTIU,
  input  [3:0] ctrl,
  input  SLTI,
  input  I,
  input  clck,
  input  SLTU,
  input  SLT,
  input  skip,
  input  LUI,
  input  MOVN,
  input  MOVZ,
  input  [31:0] PCPlus4,
  input  [4:0] rd,
  input  [4:0] rt,
  input  [4:0] rs,
  output [31:0] Aout,
  output [31:0] Bout,
  output [4:0] SaOut,
  output [31:0] immOut,
  output SLTIUout,
  output [3:0] ctrlOut,
  output SLTIout,
  output Iout,
  output SLTUout,
  output SLTout,
  output skipOut,
  output LUIout,
  output MOVNout,
  output MOVZout,
  output [4:0] rdOut,
  output [4:0] rtOut,
  output [4:0] rsOut
);

  Register #(.width(32)) register_1 (.D(A), .clk(clck), .Q(Aout));  // open: en, clr
  Register #(.width(32)) register_2 (.D(B), .clk(clck), .Q(Bout));  // open: en, clr
  Register #(.width(5)) register_3 (.D(Sa), .clk(clck), .Q(SaOut));  // open: en, clr
  Register #(.width(32)) register_4 (.D(imm), .clk(clck), .Q(immOut));  // open: en, clr
  Register #(.width(1)) register_5 (.D(SLTIU), .clk(clck), .Q(SLTIUout));  // open: en, clr
  Register #(.width(4)) register_6 (.D(ctrl), .clk(clck), .Q(ctrlOut));  // open: en, clr
  Register #(.width(1)) register_7 (.D(SLTI), .clk(clck), .Q(SLTIout));  // open: en, clr
  Register #(.width(1)) register_8 (.D(I), .clk(clck), .Q(Iout));  // open: en, clr
  Register #(.width(1)) register_9 (.D(SLTU), .clk(clck), .Q(SLTUout));  // open: en, clr
  Register #(.width(1)) register_10 (.D(SLT), .clk(clck), .Q(SLTout));  // open: en, clr
  Register #(.width(1)) register_11 (.D(skip), .clk(clck), .Q(skipOut));  // open: en, clr
  Register #(.width(1)) register_12 (.D(LUI), .clk(clck), .Q(LUIout));  // open: en, clr
  Register #(.width(1)) register_13 (.D(MOVN), .clk(clck), .Q(MOVNout));  // open: en, clr
  Register #(.width(1)) register_14 (.D(MOVZ), .clk(clck), .Q(MOVZout));  // open: en, clr
  Register #(.width(32)) register_15 (.D(PCPlus4), .clk(clck));  // open: en, Q, clr
  Register #(.width(5)) register_16 (.D(rd), .clk(clck), .Q(rdOut));  // open: en, clr
  Register #(.width(5)) register_17 (.D(rt), .clk(clck), .Q(rtOut));  // open: en, clr
  Register #(.width(5)) register_18 (.D(rs), .clk(clck), .Q(rsOut));  // open: en, clr
endmodule

module IFID (
  input  [31:0] inst,
  input  [31:0] PCPlus4,
  input  clck,
  output [31:0] instOut,
  output [31:0] PCPlus4Out
);

  Register #(.width(32)) register_1 (.D(inst), .clk(clck), .Q(instOut));  // open: en, clr
  Register #(.width(32)) register_2 (.D(PCPlus4), .clk(clck), .Q(PCPlus4Out));  // open: en, clr
endmodule

module instructionMemory (
  input  [31:0] A,
  input  [31:0] D,
  input  move,
  input  skip,
  input  [4:0] rd,
  output [31:0] Aout,
  output [31:0] Dout,
  output moveOut,
  output skipOut,
  output [4:0] rdOut
);


  assign Aout = A;
  assign Dout = D;
  assign moveOut = move;
  assign rdOut = rd;
  assign skipOut = skip;
endmodule

module instrcutionWriteback (
  input  [31:0] A,
  input  [31:0] D,
  input  move,
  input  [4:0] rd,
  input  skip,
  output [31:0] result,
  output [4:0] rdOut,
  output WE
);

  not not_1 (WE, skip);
  Multiplexer #(.width(32), .enable("false")) multiplexer_1 (.in0(D), .in1(A), .out(result), .sel(move));

  assign rdOut = rd;
endmodule

module EXMEM (
  input  [31:0] A,
  input  [31:0] D,
  input  clck,
  input  move,
  input  skip,
  input  [4:0] rd,
  output [31:0] Aout,
  output [31:0] Dout,
  output moveOut,
  output skipOut,
  output [4:0] rdOut
);

  Register #(.width(32)) register_1 (.D(A), .clk(clck), .Q(Aout));  // open: en, clr
  Register #(.width(32)) register_2 (.D(D), .clk(clck), .Q(Dout));  // open: en, clr
  Register #(.width(1)) register_3 (.D(move), .clk(clck), .Q(moveOut));  // open: en, clr
  Register #(.width(1)) register_4 (.D(skip), .clk(clck), .Q(skipOut));  // open: en, clr
  Register #(.width(5)) register_5 (.D(rd), .clk(clck), .Q(rdOut));  // open: en, clr
endmodule

module MEMWB (
  input  [31:0] A,
  input  [31:0] D,
  input  clck,
  input  move,
  input  skip,
  input  [4:0] rd,
  output [31:0] Aout,
  output [31:0] Dout,
  output moveOut,
  output skipOut,
  output [4:0] rdOut
);

  Register #(.width(32)) register_1 (.D(A), .clk(clck), .Q(Aout));  // open: en, clr
  Register #(.width(32)) register_2 (.D(D), .clk(clck), .Q(Dout));  // open: en, clr
  Register #(.width(1)) register_3 (.D(move), .clk(clck), .Q(moveOut));  // open: en, clr
  Register #(.width(1)) register_4 (.D(skip), .clk(clck), .Q(skipOut));  // open: en, clr
  Register #(.width(5)) register_5 (.D(rd), .clk(clck), .Q(rdOut));  // open: en, clr
endmodule

module Hazards (
  input  [4:0] IDEXrt,
  input  [4:0] IDEXrs,
  input  [4:0] EXMEMrd,
  input  EXMEMregWrite,
  input  [4:0] MEMWBrd,
  input  MEMWBregWrite,
  output [1:0] HazardA,
  output [1:0] HazardB
);

  wire and_1_out, and_2_out, and_3_out, and_4_out, and_5_out, and_6_out, and_9_out, and_10_out, and_11_out,
       and_12_out, neq_1_o, neq_2_o, not_1_out;
  wire [4:0] xnor_1_out, xnor_2_out, xnor_3_out, xnor_4_out;

  neq neq_1 (.i(EXMEMrd), .O(neq_1_o));
  assign xnor_1_out = ~(IDEXrs ^ MEMWBrd);  // XNOR_Gate xnor_1, 5 bits wide
  assign xnor_2_out = ~(IDEXrt ^ MEMWBrd);  // XNOR_Gate xnor_2, 5 bits wide
  assign xnor_3_out = ~(IDEXrt ^ EXMEMrd);  // XNOR_Gate xnor_3, 5 bits wide
  assign xnor_4_out = ~(IDEXrs ^ EXMEMrd);  // XNOR_Gate xnor_4, 5 bits wide
  and and_1 (and_1_out, neq_1_o, EXMEMregWrite);
  neq neq_2 (.i(MEMWBrd), .O(neq_2_o));
  and and_2 (and_2_out, xnor_3_out[0], xnor_3_out[1], xnor_3_out[2], xnor_3_out[3], xnor_3_out[4]);
  not not_1 (not_1_out, and_1_out);
  and and_3 (and_3_out, MEMWBregWrite, neq_2_o);
  and and_4 (and_4_out, xnor_1_out[0], xnor_1_out[1], xnor_1_out[2], xnor_1_out[3], xnor_1_out[4]);
  and and_5 (and_5_out, xnor_2_out[0], xnor_2_out[1], xnor_2_out[2], xnor_2_out[3], xnor_2_out[4]);
  and and_6 (and_6_out, xnor_4_out[0], xnor_4_out[1], xnor_4_out[2], xnor_4_out[3], xnor_4_out[4]);
  and and_7 (HazardA[1], and_6_out, and_1_out);
  and and_8 (HazardB[1], and_2_out, and_1_out);
  and and_9 (and_9_out, not_1_out, and_6_out);
  and and_10 (and_10_out, and_4_out, and_3_out);
  and and_11 (and_11_out, and_2_out, not_1_out);
  and and_12 (and_12_out, and_3_out, and_5_out);
  or or_1 (HazardA[0], and_9_out, and_10_out);
  or or_2 (HazardB[0], and_11_out, and_12_out);
endmodule

module neq (
  input  [4:0] i,
  output O
);

  or or_1 (O, i[0], i[1], i[2], i[3], i[4]);
endmodule
